// Logisim project cpu1.circ as structural Verilog: 7 circuits, main circuit ULA
module ULA (
  input  A,
  input  C3,
  input  C2,
  input  B,
  input  C0,
  input  C1,
  input  Clock,
  output DM0,
  output DM1,
  output S1,
  output S0,
  output SR
);

  wire d_ff_1_q, d_ff_2_q, multiplexer_1_out, multiplexer_2_out, not_1_out, not_2_out, not_3_out, or_1_out,
       somador_completo_1_co, somador_completo_1_s, somador_completo_2_s, somador_completo_3_co,
       somador_completo_3_s, somador_completo_4_s;
  wire [1:0] multiplexer_3_out;

  Multiplexer #(.disabled(0), .enable("false")) multiplexer_1 (
    .in0(A), .in1(d_ff_1_q), .out(multiplexer_1_out), .sel(C0));
  Multiplexer #(.disabled(0), .enable("false")) multiplexer_2 (
    .in0(B), .in1(d_ff_2_q), .out(multiplexer_2_out), .sel(C0));
  not not_1 (not_1_out, d_ff_1_q);
  not not_2 (not_2_out, d_ff_2_q);
  Somador_Completo somador_completo_1 (
    .S(somador_completo_1_s), .Co(somador_completo_1_co), .A(multiplexer_1_out), .B(multiplexer_3_out[0]));  // open: Ci
  Somador_Completo somador_completo_2 (
    .S(somador_completo_2_s), .A(multiplexer_2_out), .B(multiplexer_3_out[1]), .Ci(somador_completo_1_co));  // open: Co
  Somador_Completo somador_completo_3 (
    .S(somador_completo_3_s), .Co(somador_completo_3_co), .A(not_1_out), .B(1'b0));  // open: Ci
  Somador_Completo somador_completo_4 (
    .S(somador_completo_4_s), .A(not_2_out), .B(1'b1), .Ci(somador_completo_3_co));  // open: Co
  D_Flip_Flop d_ff_1 (.clk(Clock), .D(S0), .Q(d_ff_1_q), .preset(1'b0), .en(1'b1), .reset(1'b0));  // open: Qn
  D_Flip_Flop d_ff_2 (.clk(Clock), .D(S1), .Q(d_ff_2_q), .preset(1'b0), .en(1'b1), .reset(1'b0));  // open: Qn
  Multiplexer #(.disabled(0), .enable("false")) multiplexer_3 (
    .in0(somador_completo_3_s), .in1(d_ff_1_q), .out(multiplexer_3_out[0]), .sel(C1));
  Multiplexer #(.disabled(0), .enable("false")) multiplexer_4 (
    .in0(somador_completo_4_s), .in1(d_ff_2_q), .out(multiplexer_3_out[1]), .sel(C1));
  or or_1 (or_1_out, d_ff_1_q, d_ff_2_q);
  Multiplexer #(.disabled(0), .enable("false")) multiplexer_5 (
    .in0(multiplexer_1_out), .in1(somador_completo_1_s), .out(S0), .sel(C2));
  Multiplexer #(.disabled(0), .enable("false")) multiplexer_6 (
    .in0(multiplexer_2_out), .in1(somador_completo_2_s), .out(S1), .sel(C2));
  not not_3 (not_3_out, or_1_out);
  D_Flip_Flop d_ff_3 (.clk(Clock), .D(not_3_out), .Q(SR), .preset(1'b0), .en(1'b1), .reset(1'b0));  // open: Qn
  Multiplexer #(.disabled(0), .enable("false")) multiplexer_7 (.in0(S0), .out(DM0), .sel(C3));  // open: in1
  Multiplexer #(.disabled(0), .enable("false")) multiplexer_8 (.in0(S1), .out(DM1), .sel(C3));  // open: in1

  // Notes on the sheet:
  //   Somador Completo
  //   SR
  //   NC
  //   NC
endmodule

module Environment (
);

  wire Clock_out, controle_1_c0, controle_1_c1, controle_1_c2, controle_1_c3, controle_1_c4,
       multiplexer_1_out, multiplexer_2_out, multiplexer_3_out, multiplexer_6_out, multiplexer_7_out,
       ULA_dm0, ULA_dm1, ULA_sr;
  wire [3:0] multiplexer_4_out, pc_1_s0;
  wire [15:0] demultiplexer_1_out0, demultiplexer_2_out0, DMEM_adout, DMEM_bdout, IMEM_i0out, IMEM_i1out,
       IMEM_i2out, IMEM_i3out, IMEM_i4out, IMEM_i5out, IMEM_i6out;

  Clock Clock (.out(Clock_out));
  PC pc_1 (
    .Clock(Clock_out), .S0(pc_1_s0[0]), .S1(pc_1_s0[1]), .S2(pc_1_s0[2]), .S3(pc_1_s0[3]),
    .C4(controle_1_c4), .I3(multiplexer_4_out[0]), .I5(multiplexer_4_out[2]), .I4(multiplexer_4_out[1]),
    .I6(multiplexer_4_out[3]));  // open: Preset, Enable, Clear
  IMEM IMEM (
    .I0OUT(IMEM_i0out), .I1OUT(IMEM_i1out), .I2OUT(IMEM_i2out), .Clock(Clock_out), .Preset(1'b0),
    .Clear(1'b0), .I3OUT(IMEM_i3out), .I4OUT(IMEM_i4out), .I6OUT(IMEM_i6out), .I5OUT(IMEM_i5out));  // open: I0IN, I2IN, Enable, I3IN, I4IN, I5IN, I6IN, I1IN
  DMEM DMEM (
    .BDOUT(DMEM_bdout), .ADIN(demultiplexer_1_out0), .BDIN(demultiplexer_2_out0), .ADOUT(DMEM_adout),
    .Clock(Clock_out));  // open: Preset, Enable, Clear
  Multiplexer #(.select(4), .disabled(0), .enable("false")) multiplexer_1 (
    .in0(IMEM_i0out[0]), .in1(IMEM_i0out[1]), .in2(IMEM_i0out[2]), .in3(IMEM_i0out[3]), .in4(IMEM_i0out[4]),
    .in5(IMEM_i0out[5]), .in6(IMEM_i0out[6]), .in7(IMEM_i0out[7]), .in8(IMEM_i0out[8]), .in9(IMEM_i0out[9]),
    .in10(IMEM_i0out[10]), .in11(IMEM_i0out[11]), .in12(IMEM_i0out[12]), .in13(IMEM_i0out[13]),
    .in14(IMEM_i0out[14]), .in15(IMEM_i0out[15]), .out(multiplexer_1_out), .sel(pc_1_s0));
  Multiplexer #(.select(4), .disabled(0), .enable("false")) multiplexer_2 (
    .in0(IMEM_i1out[0]), .in1(IMEM_i1out[1]), .in2(IMEM_i1out[2]), .in3(IMEM_i1out[3]), .in4(IMEM_i1out[4]),
    .in5(IMEM_i1out[5]), .in6(IMEM_i1out[6]), .in7(IMEM_i1out[7]), .in8(IMEM_i1out[8]), .in9(IMEM_i1out[9]),
    .in10(IMEM_i1out[10]), .in11(IMEM_i1out[11]), .in12(IMEM_i1out[12]), .in13(IMEM_i1out[13]),
    .in14(IMEM_i1out[14]), .in15(IMEM_i1out[15]), .out(multiplexer_2_out), .sel(pc_1_s0));
  Multiplexer #(.select(4), .disabled(0), .enable("false")) multiplexer_3 (
    .in0(IMEM_i2out[0]), .in1(IMEM_i2out[1]), .in2(IMEM_i2out[2]), .in3(IMEM_i2out[3]), .in4(IMEM_i2out[4]),
    .in5(IMEM_i2out[5]), .in6(IMEM_i2out[6]), .in7(IMEM_i2out[7]), .in8(IMEM_i2out[8]), .in9(IMEM_i2out[9]),
    .in10(IMEM_i2out[10]), .in11(IMEM_i2out[11]), .in12(IMEM_i2out[12]), .in13(IMEM_i2out[13]),
    .in14(IMEM_i2out[14]), .in15(IMEM_i2out[15]), .out(multiplexer_3_out), .sel(pc_1_s0));
  Multiplexer #(.select(4), .disabled(0), .enable("false")) multiplexer_4 (
    .in0(IMEM_i3out[0]), .in1(IMEM_i3out[1]), .in2(IMEM_i3out[2]), .in3(IMEM_i3out[3]), .in4(IMEM_i3out[4]),
    .in5(IMEM_i3out[5]), .in6(IMEM_i3out[6]), .in7(IMEM_i3out[7]), .in8(IMEM_i3out[8]), .in9(IMEM_i3out[9]),
    .in10(IMEM_i3out[10]), .in11(IMEM_i3out[11]), .in12(IMEM_i3out[12]), .in13(IMEM_i3out[13]),
    .in14(IMEM_i3out[14]), .in15(IMEM_i3out[15]), .out(multiplexer_4_out[0]), .sel(pc_1_s0));
  Multiplexer #(.select(4), .disabled(0), .enable("false")) multiplexer_5 (
    .in0(IMEM_i4out[0]), .in1(IMEM_i4out[1]), .in2(IMEM_i4out[2]), .in3(IMEM_i4out[3]), .in4(IMEM_i4out[4]),
    .in5(IMEM_i4out[5]), .in6(IMEM_i4out[6]), .in7(IMEM_i4out[7]), .in8(IMEM_i4out[8]), .in9(IMEM_i4out[9]),
    .in10(IMEM_i4out[10]), .in11(IMEM_i4out[11]), .in12(IMEM_i4out[12]), .in13(IMEM_i4out[13]),
    .in14(IMEM_i4out[14]), .in15(IMEM_i4out[15]), .out(multiplexer_4_out[1]), .sel(pc_1_s0));
  Multiplexer #(.select(4), .disabled(0), .enable("false")) multiplexer_6 (
    .in0(DMEM_adout[0]), .in1(DMEM_adout[1]), .in2(DMEM_adout[2]), .in3(DMEM_adout[3]), .in4(DMEM_adout[4]),
    .in5(DMEM_adout[5]), .in6(DMEM_adout[6]), .in7(DMEM_adout[7]), .in8(DMEM_adout[8]), .in9(DMEM_adout[9]),
    .in10(DMEM_adout[10]), .in11(DMEM_adout[11]), .in12(DMEM_adout[12]), .in13(DMEM_adout[13]),
    .in14(DMEM_adout[14]), .in15(DMEM_adout[15]), .out(multiplexer_6_out), .sel(multiplexer_4_out));
  Multiplexer #(.select(4), .disabled(0), .enable("false")) multiplexer_7 (
    .in0(DMEM_bdout[0]), .in1(DMEM_bdout[1]), .in2(DMEM_bdout[2]), .in3(DMEM_bdout[3]), .in4(DMEM_bdout[4]),
    .in5(DMEM_bdout[5]), .in6(DMEM_bdout[6]), .in7(DMEM_bdout[7]), .in8(DMEM_bdout[8]), .in9(DMEM_bdout[9]),
    .in10(DMEM_bdout[10]), .in11(DMEM_bdout[11]), .in12(DMEM_bdout[12]), .in13(DMEM_bdout[13]),
    .in14(DMEM_bdout[14]), .in15(DMEM_bdout[15]), .out(multiplexer_7_out), .sel(multiplexer_4_out));
  Multiplexer #(.select(4), .disabled(0), .enable("false")) multiplexer_8 (
    .in0(IMEM_i5out[0]), .in1(IMEM_i5out[1]), .in2(IMEM_i5out[2]), .in3(IMEM_i5out[3]), .in4(IMEM_i5out[4]),
    .in5(IMEM_i5out[5]), .in6(IMEM_i5out[6]), .in7(IMEM_i5out[7]), .in8(IMEM_i5out[8]), .in9(IMEM_i5out[9]),
    .in10(IMEM_i5out[10]), .in11(IMEM_i5out[11]), .in12(IMEM_i5out[12]), .in13(IMEM_i5out[13]),
    .in14(IMEM_i5out[14]), .in15(IMEM_i5out[15]), .out(multiplexer_4_out[2]), .sel(pc_1_s0));
  Multiplexer #(.select(4), .disabled(0), .enable("false")) multiplexer_9 (
    .in0(IMEM_i6out[0]), .in1(IMEM_i6out[1]), .in2(IMEM_i6out[2]), .in3(IMEM_i6out[3]), .in4(IMEM_i6out[4]),
    .in5(IMEM_i6out[5]), .in6(IMEM_i6out[6]), .in7(IMEM_i6out[7]), .in8(IMEM_i6out[8]), .in9(IMEM_i6out[9]),
    .in10(IMEM_i6out[10]), .in11(IMEM_i6out[11]), .in12(IMEM_i6out[12]), .in13(IMEM_i6out[13]),
    .in14(IMEM_i6out[14]), .in15(IMEM_i6out[15]), .out(multiplexer_4_out[3]), .sel(pc_1_s0));
  ULA ULA (
    .A(multiplexer_6_out), .B(multiplexer_7_out), .C0(controle_1_c0), .C1(controle_1_c1), .C2(controle_1_c2),
    .C3(controle_1_c3), .SR(ULA_sr), .DM0(ULA_dm0), .DM1(ULA_dm1), .Clock(Clock_out));  // open: S1, S0
  Demultiplexer #(.select(4), .tristate("true"), .enable("false")) demultiplexer_1 (
    .out0(demultiplexer_1_out0[0]), .out1(demultiplexer_1_out0[1]), .out2(demultiplexer_1_out0[2]),
    .out3(demultiplexer_1_out0[3]), .out4(demultiplexer_1_out0[4]), .out5(demultiplexer_1_out0[5]),
    .out6(demultiplexer_1_out0[6]), .out7(demultiplexer_1_out0[7]), .out8(demultiplexer_1_out0[8]),
    .out9(demultiplexer_1_out0[9]), .out10(demultiplexer_1_out0[10]), .out11(demultiplexer_1_out0[11]),
    .out12(demultiplexer_1_out0[12]), .out13(demultiplexer_1_out0[13]), .out14(demultiplexer_1_out0[14]),
    .out15(demultiplexer_1_out0[15]), .in(ULA_dm0), .sel(multiplexer_4_out));
  Demultiplexer #(.select(4), .tristate("true"), .enable("false")) demultiplexer_2 (
    .out0(demultiplexer_2_out0[0]), .out1(demultiplexer_2_out0[1]), .out2(demultiplexer_2_out0[2]),
    .out3(demultiplexer_2_out0[3]), .out4(demultiplexer_2_out0[4]), .out5(demultiplexer_2_out0[5]),
    .out6(demultiplexer_2_out0[6]), .out7(demultiplexer_2_out0[7]), .out8(demultiplexer_2_out0[8]),
    .out9(demultiplexer_2_out0[9]), .out10(demultiplexer_2_out0[10]), .out11(demultiplexer_2_out0[11]),
    .out12(demultiplexer_2_out0[12]), .out13(demultiplexer_2_out0[13]), .out14(demultiplexer_2_out0[14]),
    .out15(demultiplexer_2_out0[15]), .in(ULA_dm1), .sel(multiplexer_4_out));
  Controle controle_1 (
    .SR(ULA_sr), .C0(controle_1_c0), .C1(controle_1_c1), .C2(controle_1_c2), .C3(controle_1_c3),
    .C4(controle_1_c4), .I0(multiplexer_1_out), .I1(multiplexer_2_out), .I2(multiplexer_3_out));

  // Notes on the sheet:
  //   PC
  //   Opcional
  //   Controle
endmodule

module DMEM (
  input  [15:0] ADIN,
  input  [15:0] BDIN,
  input  Clock,
  input  Clear,
  input  Enable,
  input  Preset,
  output [15:0] ADOUT,
  output [15:0] BDOUT
);

  D_Flip_Flop d_ff_1 (.clk(Clock), .D(ADIN[0]), .Q(ADOUT[0]), .preset(Preset), .en(Enable), .reset(Clear));  // open: Qn
  D_Flip_Flop d_ff_2 (.clk(Clock), .D(ADIN[1]), .Q(ADOUT[1]), .preset(Preset), .en(Enable), .reset(Clear));  // open: Qn
  D_Flip_Flop d_ff_3 (.clk(Clock), .D(ADIN[2]), .Q(ADOUT[2]), .preset(Preset), .en(Enable), .reset(Clear));  // open: Qn
  D_Flip_Flop d_ff_4 (.clk(Clock), .D(ADIN[3]), .Q(ADOUT[3]), .preset(Preset), .en(Enable), .reset(Clear));  // open: Qn
  D_Flip_Flop d_ff_5 (.clk(Clock), .D(ADIN[4]), .Q(ADOUT[4]), .preset(Preset), .en(Enable), .reset(Clear));  // open: Qn
  D_Flip_Flop d_ff_6 (.clk(Clock), .D(ADIN[5]), .Q(ADOUT[5]), .preset(Preset), .en(Enable), .reset(Clear));  // open: Qn
  D_Flip_Flop d_ff_7 (.clk(Clock), .D(ADIN[6]), .Q(ADOUT[6]), .preset(Preset), .en(Enable), .reset(Clear));  // open: Qn
  D_Flip_Flop d_ff_8 (.clk(Clock), .D(ADIN[7]), .Q(ADOUT[7]), .preset(Preset), .en(Enable), .reset(Clear));  // open: Qn
  D_Flip_Flop d_ff_9 (.clk(Clock), .D(ADIN[8]), .Q(ADOUT[8]), .preset(Preset), .en(Enable), .reset(Clear));  // open: Qn
  D_Flip_Flop d_ff_10 (
    .clk(Clock), .D(ADIN[9]), .Q(ADOUT[9]), .preset(Preset), .en(Enable), .reset(Clear));  // open: Qn
  D_Flip_Flop d_ff_11 (
    .clk(Clock), .D(ADIN[10]), .Q(ADOUT[10]), .preset(Preset), .en(Enable), .reset(Clear));  // open: Qn
  D_Flip_Flop d_ff_12 (
    .clk(Clock), .D(ADIN[11]), .Q(ADOUT[11]), .preset(Preset), .en(Enable), .reset(Clear));  // open: Qn
  D_Flip_Flop d_ff_13 (
    .clk(Clock), .D(ADIN[12]), .Q(ADOUT[12]), .preset(Preset), .en(Enable), .reset(Clear));  // open: Qn
  D_Flip_Flop d_ff_14 (
    .clk(Clock), .D(ADIN[13]), .Q(ADOUT[13]), .preset(Preset), .en(Enable), .reset(Clear));  // open: Qn
  D_Flip_Flop d_ff_15 (
    .clk(Clock), .D(ADIN[14]), .Q(ADOUT[14]), .preset(Preset), .en(Enable), .reset(Clear));  // open: Qn
  D_Flip_Flop d_ff_16 (
    .clk(Clock), .D(ADIN[15]), .Q(ADOUT[15]), .preset(Preset), .en(Enable), .reset(Clear));  // open: Qn
  D_Flip_Flop d_ff_17 (
    .clk(Clock), .D(BDIN[0]), .Q(BDOUT[0]), .preset(Preset), .en(Enable), .reset(Clear));  // open: Qn
  D_Flip_Flop d_ff_18 (
    .clk(Clock), .D(BDIN[1]), .Q(BDOUT[1]), .preset(Preset), .en(Enable), .reset(Clear));  // open: Qn
  D_Flip_Flop d_ff_19 (
    .clk(Clock), .D(BDIN[2]), .Q(BDOUT[2]), .preset(Preset), .en(Enable), .reset(Clear));  // open: Qn
  D_Flip_Flop d_ff_20 (
    .clk(Clock), .D(BDIN[3]), .Q(BDOUT[3]), .preset(Preset), .en(Enable), .reset(Clear));  // open: Qn
  D_Flip_Flop d_ff_21 (
    .clk(Clock), .D(BDIN[4]), .Q(BDOUT[4]), .preset(Preset), .en(Enable), .reset(Clear));  // open: Qn
  D_Flip_Flop d_ff_22 (
    .clk(Clock), .D(BDIN[5]), .Q(BDOUT[5]), .preset(Preset), .en(Enable), .reset(Clear));  // open: Qn
  D_Flip_Flop d_ff_23 (
    .clk(Clock), .D(BDIN[6]), .Q(BDOUT[6]), .preset(Preset), .en(Enable), .reset(Clear));  // open: Qn
  D_Flip_Flop d_ff_24 (
    .clk(Clock), .D(BDIN[7]), .Q(BDOUT[7]), .preset(Preset), .en(Enable), .reset(Clear));  // open: Qn
  D_Flip_Flop d_ff_25 (
    .clk(Clock), .D(BDIN[8]), .Q(BDOUT[8]), .preset(Preset), .en(Enable), .reset(Clear));  // open: Qn
  D_Flip_Flop d_ff_26 (
    .clk(Clock), .D(BDIN[9]), .Q(BDOUT[9]), .preset(Preset), .en(Enable), .reset(Clear));  // open: Qn
  D_Flip_Flop d_ff_27 (
    .clk(Clock), .D(BDIN[10]), .Q(BDOUT[10]), .preset(Preset), .en(Enable), .reset(Clear));  // open: Qn
  D_Flip_Flop d_ff_28 (
    .clk(Clock), .D(BDIN[11]), .Q(BDOUT[11]), .preset(Preset), .en(Enable), .reset(Clear));  // open: Qn
  D_Flip_Flop d_ff_29 (
    .clk(Clock), .D(BDIN[12]), .Q(BDOUT[12]), .preset(Preset), .en(Enable), .reset(Clear));  // open: Qn
  D_Flip_Flop d_ff_30 (
    .clk(Clock), .D(BDIN[13]), .Q(BDOUT[13]), .preset(Preset), .en(Enable), .reset(Clear));  // open: Qn
  D_Flip_Flop d_ff_31 (
    .clk(Clock), .D(BDIN[14]), .Q(BDOUT[14]), .preset(Preset), .en(Enable), .reset(Clear));  // open: Qn
  D_Flip_Flop d_ff_32 (
    .clk(Clock), .D(BDIN[15]), .Q(BDOUT[15]), .preset(Preset), .en(Enable), .reset(Clear));  // open: Qn
endmodule

module IMEM (
  input  [15:0] I0IN,
  input  [15:0] I2IN,
  input  [15:0] I3IN,
  input  [15:0] I5IN,
  input  [15:0] I1IN,
  input  [15:0] I4IN,
  input  [15:0] I6IN,
  input  Clock,
  input  Clear,
  input  Enable,
  input  Preset,
  output [15:0] I0OUT,
  output [15:0] I3OUT,
  output [15:0] I5OUT,
  output [15:0] I1OUT,
  output [15:0] I2OUT,
  output [15:0] I4OUT,
  output [15:0] I6OUT
);

  wire [15:0] undriven;

  D_Flip_Flop d_ff_1 (.clk(Clock), .D(I0IN[0]), .Q(I0OUT[0]), .preset(Preset), .en(Enable), .reset(Clear));  // open: Qn
  D_Flip_Flop d_ff_2 (.clk(Clock), .D(I0IN[1]), .Q(I0OUT[1]), .preset(Preset), .en(Enable), .reset(Clear));  // open: Qn
  D_Flip_Flop d_ff_3 (.clk(Clock), .D(I0IN[2]), .Q(I0OUT[2]), .preset(Preset), .en(Enable), .reset(Clear));  // open: Qn
  D_Flip_Flop d_ff_4 (.clk(Clock), .D(I0IN[3]), .Q(I0OUT[3]), .preset(Preset), .en(Enable), .reset(Clear));  // open: Qn
  D_Flip_Flop d_ff_5 (.clk(Clock), .D(I0IN[4]), .Q(I0OUT[4]), .preset(Preset), .en(Enable), .reset(Clear));  // open: Qn
  D_Flip_Flop d_ff_6 (.clk(Clock), .D(I0IN[5]), .Q(I0OUT[5]), .preset(Preset), .en(Enable), .reset(Clear));  // open: Qn
  D_Flip_Flop d_ff_7 (.clk(Clock), .D(I0IN[6]), .Q(I0OUT[6]), .preset(Preset), .en(Enable), .reset(Clear));  // open: Qn
  D_Flip_Flop d_ff_8 (.clk(Clock), .D(I0IN[7]), .Q(I0OUT[7]), .preset(Preset), .en(Enable), .reset(Clear));  // open: Qn
  D_Flip_Flop d_ff_9 (.clk(Clock), .D(I0IN[8]), .Q(I0OUT[8]), .preset(Preset), .en(Enable), .reset(Clear));  // open: Qn
  D_Flip_Flop d_ff_10 (
    .clk(Clock), .D(I0IN[9]), .Q(I0OUT[9]), .preset(Preset), .en(Enable), .reset(Clear));  // open: Qn
  D_Flip_Flop d_ff_11 (
    .clk(Clock), .D(I0IN[10]), .Q(I0OUT[10]), .preset(Preset), .en(Enable), .reset(Clear));  // open: Qn
  D_Flip_Flop d_ff_12 (
    .clk(Clock), .D(I0IN[11]), .Q(I0OUT[11]), .preset(Preset), .en(Enable), .reset(Clear));  // open: Qn
  D_Flip_Flop d_ff_13 (
    .clk(Clock), .D(I0IN[12]), .Q(I0OUT[12]), .preset(Preset), .en(Enable), .reset(Clear));  // open: Qn
  D_Flip_Flop d_ff_14 (
    .clk(Clock), .D(I0IN[13]), .Q(I0OUT[13]), .preset(Preset), .en(Enable), .reset(Clear));  // open: Qn
  D_Flip_Flop d_ff_15 (
    .clk(Clock), .D(I0IN[14]), .Q(I0OUT[14]), .preset(Preset), .en(Enable), .reset(Clear));  // open: Qn
  D_Flip_Flop d_ff_16 (
    .clk(Clock), .D(I0IN[15]), .Q(I0OUT[15]), .preset(Preset), .en(Enable), .reset(Clear));  // open: Qn
  D_Flip_Flop d_ff_17 (
    .clk(Clock), .D(undriven[0]), .Q(I1OUT[0]), .preset(Preset), .en(Enable), .reset(Clear));  // open: Qn
  D_Flip_Flop d_ff_18 (
    .clk(Clock), .D(undriven[1]), .Q(I1OUT[1]), .preset(Preset), .en(Enable), .reset(Clear));  // open: Qn
  D_Flip_Flop d_ff_19 (
    .clk(Clock), .D(undriven[2]), .Q(I1OUT[2]), .preset(Preset), .en(Enable), .reset(Clear));  // open: Qn
  D_Flip_Flop d_ff_20 (
    .clk(Clock), .D(undriven[3]), .Q(I1OUT[3]), .preset(Preset), .en(Enable), .reset(Clear));  // open: Qn
  D_Flip_Flop d_ff_21 (
    .clk(Clock), .D(undriven[4]), .Q(I1OUT[4]), .preset(Preset), .en(Enable), .reset(Clear));  // open: Qn
  D_Flip_Flop d_ff_22 (
    .clk(Clock), .D(undriven[5]), .Q(I1OUT[5]), .preset(Preset), .en(Enable), .reset(Clear));  // open: Qn
  D_Flip_Flop d_ff_23 (
    .clk(Clock), .D(undriven[6]), .Q(I1OUT[6]), .preset(Preset), .en(Enable), .reset(Clear));  // open: Qn
  D_Flip_Flop d_ff_24 (
    .clk(Clock), .D(undriven[7]), .Q(I1OUT[7]), .preset(Preset), .en(Enable), .reset(Clear));  // open: Qn
  D_Flip_Flop d_ff_25 (
    .clk(Clock), .D(undriven[8]), .Q(I1OUT[8]), .preset(Preset), .en(Enable), .reset(Clear));  // open: Qn
  D_Flip_Flop d_ff_26 (
    .clk(Clock), .D(undriven[9]), .Q(I1OUT[9]), .preset(Preset), .en(Enable), .reset(Clear));  // open: Qn
  D_Flip_Flop d_ff_27 (
    .clk(Clock), .D(undriven[10]), .Q(I1OUT[10]), .preset(Preset), .en(Enable), .reset(Clear));  // open: Qn
  D_Flip_Flop d_ff_28 (
    .clk(Clock), .D(undriven[11]), .Q(I1OUT[11]), .preset(Preset), .en(Enable), .reset(Clear));  // open: Qn
  D_Flip_Flop d_ff_29 (
    .clk(Clock), .D(undriven[12]), .Q(I1OUT[12]), .preset(Preset), .en(Enable), .reset(Clear));  // open: Qn
  D_Flip_Flop d_ff_30 (
    .clk(Clock), .D(undriven[13]), .Q(I1OUT[13]), .preset(Preset), .en(Enable), .reset(Clear));  // open: Qn
  D_Flip_Flop d_ff_31 (
    .clk(Clock), .D(undriven[14]), .Q(I1OUT[14]), .preset(Preset), .en(Enable), .reset(Clear));  // open: Qn
  D_Flip_Flop d_ff_32 (
    .clk(Clock), .D(undriven[15]), .Q(I1OUT[15]), .preset(Preset), .en(Enable), .reset(Clear));  // open: Qn
  D_Flip_Flop d_ff_33 (
    .clk(Clock), .D(I2IN[0]), .Q(I2OUT[0]), .preset(Preset), .en(Enable), .reset(Clear));  // open: Qn
  D_Flip_Flop d_ff_34 (
    .clk(Clock), .D(I2IN[1]), .Q(I2OUT[1]), .preset(Preset), .en(Enable), .reset(Clear));  // open: Qn
  D_Flip_Flop d_ff_35 (
    .clk(Clock), .D(I2IN[2]), .Q(I2OUT[2]), .preset(Preset), .en(Enable), .reset(Clear));  // open: Qn
  D_Flip_Flop d_ff_36 (
    .clk(Clock), .D(I2IN[3]), .Q(I2OUT[3]), .preset(Preset), .en(Enable), .reset(Clear));  // open: Qn
  D_Flip_Flop d_ff_37 (
    .clk(Clock), .D(I2IN[4]), .Q(I2OUT[4]), .preset(Preset), .en(Enable), .reset(Clear));  // open: Qn
  D_Flip_Flop d_ff_38 (
    .clk(Clock), .D(I2IN[5]), .Q(I2OUT[5]), .preset(Preset), .en(Enable), .reset(Clear));  // open: Qn
  D_Flip_Flop d_ff_39 (
    .clk(Clock), .D(I2IN[6]), .Q(I2OUT[6]), .preset(Preset), .en(Enable), .reset(Clear));  // open: Qn
  D_Flip_Flop d_ff_40 (
    .clk(Clock), .D(I2IN[7]), .Q(I2OUT[7]), .preset(Preset), .en(Enable), .reset(Clear));  // open: Qn
  D_Flip_Flop d_ff_41 (
    .clk(Clock), .D(I2IN[8]), .Q(I2OUT[8]), .preset(Preset), .en(Enable), .reset(Clear));  // open: Qn
  D_Flip_Flop d_ff_42 (
    .clk(Clock), .D(I2IN[9]), .Q(I2OUT[9]), .preset(Preset), .en(Enable), .reset(Clear));  // open: Qn
  D_Flip_Flop d_ff_43 (
    .clk(Clock), .D(I2IN[10]), .Q(I2OUT[10]), .preset(Preset), .en(Enable), .reset(Clear));  // open: Qn
  D_Flip_Flop d_ff_44 (
    .clk(Clock), .D(I2IN[11]), .Q(I2OUT[11]), .preset(Preset), .en(Enable), .reset(Clear));  // open: Qn
  D_Flip_Flop d_ff_45 (
    .clk(Clock), .D(I2IN[12]), .Q(I2OUT[12]), .preset(Preset), .en(Enable), .reset(Clear));  // open: Qn
  D_Flip_Flop d_ff_46 (
    .clk(Clock), .D(I2IN[13]), .Q(I2OUT[13]), .preset(Preset), .en(Enable), .reset(Clear));  // open: Qn
  D_Flip_Flop d_ff_47 (
    .clk(Clock), .D(I2IN[14]), .Q(I2OUT[14]), .preset(Preset), .en(Enable), .reset(Clear));  // open: Qn
  D_Flip_Flop d_ff_48 (
    .clk(Clock), .D(I2IN[15]), .Q(I2OUT[15]), .preset(Preset), .en(Enable), .reset(Clear));  // open: Qn
  D_Flip_Flop d_ff_49 (
    .clk(Clock), .D(I3IN[0]), .Q(I3OUT[0]), .preset(Preset), .en(Enable), .reset(Clear));  // open: Qn
  D_Flip_Flop d_ff_50 (
    .clk(Clock), .D(I3IN[1]), .Q(I3OUT[1]), .preset(Preset), .en(Enable), .reset(Clear));  // open: Qn
  D_Flip_Flop d_ff_51 (
    .clk(Clock), .D(I3IN[2]), .Q(I3OUT[2]), .preset(Preset), .en(Enable), .reset(Clear));  // open: Qn
  D_Flip_Flop d_ff_52 (
    .clk(Clock), .D(I3IN[3]), .Q(I3OUT[3]), .preset(Preset), .en(Enable), .reset(Clear));  // open: Qn
  D_Flip_Flop d_ff_53 (
    .clk(Clock), .D(I3IN[4]), .Q(I3OUT[4]), .preset(Preset), .en(Enable), .reset(Clear));  // open: Qn
  D_Flip_Flop d_ff_54 (
    .clk(Clock), .D(I3IN[5]), .Q(I3OUT[5]), .preset(Preset), .en(Enable), .reset(Clear));  // open: Qn
  D_Flip_Flop d_ff_55 (
    .clk(Clock), .D(I3IN[6]), .Q(I3OUT[6]), .preset(Preset), .en(Enable), .reset(Clear));  // open: Qn
  D_Flip_Flop d_ff_56 (
    .clk(Clock), .D(I3IN[7]), .Q(I3OUT[7]), .preset(Preset), .en(Enable), .reset(Clear));  // open: Qn
  D_Flip_Flop d_ff_57 (
    .clk(Clock), .D(I3IN[8]), .Q(I3OUT[8]), .preset(Preset), .en(Enable), .reset(Clear));  // open: Qn
  D_Flip_Flop d_ff_58 (
    .clk(Clock), .D(I3IN[9]), .Q(I3OUT[9]), .preset(Preset), .en(Enable), .reset(Clear));  // open: Qn
  D_Flip_Flop d_ff_59 (
    .clk(Clock), .D(I3IN[10]), .Q(I3OUT[10]), .preset(Preset), .en(Enable), .reset(Clear));  // open: Qn
  D_Flip_Flop d_ff_60 (
    .clk(Clock), .D(I3IN[11]), .Q(I3OUT[11]), .preset(Preset), .en(Enable), .reset(Clear));  // open: Qn
  D_Flip_Flop d_ff_61 (
    .clk(Clock), .D(I3IN[12]), .Q(I3OUT[12]), .preset(Preset), .en(Enable), .reset(Clear));  // open: Qn
  D_Flip_Flop d_ff_62 (
    .clk(Clock), .D(I3IN[13]), .Q(I3OUT[13]), .preset(Preset), .en(Enable), .reset(Clear));  // open: Qn
  D_Flip_Flop d_ff_63 (
    .clk(Clock), .D(I3IN[14]), .Q(I3OUT[14]), .preset(Preset), .en(Enable), .reset(Clear));  // open: Qn
  D_Flip_Flop d_ff_64 (
    .clk(Clock), .D(I3IN[15]), .Q(I3OUT[15]), .preset(Preset), .en(Enable), .reset(Clear));  // open: Qn
  D_Flip_Flop d_ff_65 (
    .clk(Clock), .D(I4IN[0]), .Q(I4OUT[0]), .preset(Preset), .en(Enable), .reset(Clear));  // open: Qn
  D_Flip_Flop d_ff_66 (
    .clk(Clock), .D(I4IN[1]), .Q(I4OUT[1]), .preset(Preset), .en(Enable), .reset(Clear));  // open: Qn
  D_Flip_Flop d_ff_67 (
    .clk(Clock), .D(I4IN[2]), .Q(I4OUT[2]), .preset(Preset), .en(Enable), .reset(Clear));  // open: Qn
  D_Flip_Flop d_ff_68 (
    .clk(Clock), .D(I4IN[3]), .Q(I4OUT[3]), .preset(Preset), .en(Enable), .reset(Clear));  // open: Qn
  D_Flip_Flop d_ff_69 (
    .clk(Clock), .D(I4IN[4]), .Q(I4OUT[4]), .preset(Preset), .en(Enable), .reset(Clear));  // open: Qn
  D_Flip_Flop d_ff_70 (
    .clk(Clock), .D(I4IN[5]), .Q(I4OUT[5]), .preset(Preset), .en(Enable), .reset(Clear));  // open: Qn
  D_Flip_Flop d_ff_71 (
    .clk(Clock), .D(I4IN[6]), .Q(I4OUT[6]), .preset(Preset), .en(Enable), .reset(Clear));  // open: Qn
  D_Flip_Flop d_ff_72 (
    .clk(Clock), .D(I4IN[7]), .Q(I4OUT[7]), .preset(Preset), .en(Enable), .reset(Clear));  // open: Qn
  D_Flip_Flop d_ff_73 (
    .clk(Clock), .D(I4IN[8]), .Q(I4OUT[8]), .preset(Preset), .en(Enable), .reset(Clear));  // open: Qn
  D_Flip_Flop d_ff_74 (
    .clk(Clock), .D(I4IN[9]), .Q(I4OUT[9]), .preset(Preset), .en(Enable), .reset(Clear));  // open: Qn
  D_Flip_Flop d_ff_75 (
    .clk(Clock), .D(I4IN[10]), .Q(I4OUT[10]), .preset(Preset), .en(Enable), .reset(Clear));  // open: Qn
  D_Flip_Flop d_ff_76 (
    .clk(Clock), .D(I4IN[11]), .Q(I4OUT[11]), .preset(Preset), .en(Enable), .reset(Clear));  // open: Qn
  D_Flip_Flop d_ff_77 (
    .clk(Clock), .D(I4IN[12]), .Q(I4OUT[12]), .preset(Preset), .en(Enable), .reset(Clear));  // open: Qn
  D_Flip_Flop d_ff_78 (
    .clk(Clock), .D(I4IN[13]), .Q(I4OUT[13]), .preset(Preset), .en(Enable), .reset(Clear));  // open: Qn
  D_Flip_Flop d_ff_79 (
    .clk(Clock), .D(I4IN[14]), .Q(I4OUT[14]), .preset(Preset), .en(Enable), .reset(Clear));  // open: Qn
  D_Flip_Flop d_ff_80 (
    .clk(Clock), .D(I4IN[15]), .Q(I4OUT[15]), .preset(Preset), .en(Enable), .reset(Clear));  // open: Qn
  D_Flip_Flop d_ff_81 (
    .clk(Clock), .D(I5IN[0]), .Q(I5OUT[0]), .preset(Preset), .en(Enable), .reset(Clear));  // open: Qn
  D_Flip_Flop d_ff_82 (
    .clk(Clock), .D(I5IN[1]), .Q(I5OUT[1]), .preset(Preset), .en(Enable), .reset(Clear));  // open: Qn
  D_Flip_Flop d_ff_83 (
    .clk(Clock), .D(I5IN[2]), .Q(I5OUT[2]), .preset(Preset), .en(Enable), .reset(Clear));  // open: Qn
  D_Flip_Flop d_ff_84 (
    .clk(Clock), .D(I5IN[3]), .Q(I5OUT[3]), .preset(Preset), .en(Enable), .reset(Clear));  // open: Qn
  D_Flip_Flop d_ff_85 (
    .clk(Clock), .D(I5IN[4]), .Q(I5OUT[4]), .preset(Preset), .en(Enable), .reset(Clear));  // open: Qn
  D_Flip_Flop d_ff_86 (
    .clk(Clock), .D(I5IN[5]), .Q(I5OUT[5]), .preset(Preset), .en(Enable), .reset(Clear));  // open: Qn
  D_Flip_Flop d_ff_87 (
    .clk(Clock), .D(I5IN[6]), .Q(I5OUT[6]), .preset(Preset), .en(Enable), .reset(Clear));  // open: Qn
  D_Flip_Flop d_ff_88 (
    .clk(Clock), .D(I5IN[7]), .Q(I5OUT[7]), .preset(Preset), .en(Enable), .reset(Clear));  // open: Qn
  D_Flip_Flop d_ff_89 (
    .clk(Clock), .D(I5IN[8]), .Q(I5OUT[8]), .preset(Preset), .en(Enable), .reset(Clear));  // open: Qn
  D_Flip_Flop d_ff_90 (
    .clk(Clock), .D(I5IN[9]), .Q(I5OUT[9]), .preset(Preset), .en(Enable), .reset(Clear));  // open: Qn
  D_Flip_Flop d_ff_91 (
    .clk(Clock), .D(I5IN[10]), .Q(I5OUT[10]), .preset(Preset), .en(Enable), .reset(Clear));  // open: Qn
  D_Flip_Flop d_ff_92 (
    .clk(Clock), .D(I5IN[11]), .Q(I5OUT[11]), .preset(Preset), .en(Enable), .reset(Clear));  // open: Qn
  D_Flip_Flop d_ff_93 (
    .clk(Clock), .D(I5IN[12]), .Q(I5OUT[12]), .preset(Preset), .en(Enable), .reset(Clear));  // open: Qn
  D_Flip_Flop d_ff_94 (
    .clk(Clock), .D(I5IN[13]), .Q(I5OUT[13]), .preset(Preset), .en(Enable), .reset(Clear));  // open: Qn
  D_Flip_Flop d_ff_95 (
    .clk(Clock), .D(I5IN[14]), .Q(I5OUT[14]), .preset(Preset), .en(Enable), .reset(Clear));  // open: Qn
  D_Flip_Flop d_ff_96 (
    .clk(Clock), .D(I5IN[15]), .Q(I5OUT[15]), .preset(Preset), .en(Enable), .reset(Clear));  // open: Qn
  D_Flip_Flop d_ff_97 (
    .clk(Clock), .D(I6IN[0]), .Q(I6OUT[0]), .preset(Preset), .en(Enable), .reset(Clear));  // open: Qn
  D_Flip_Flop d_ff_98 (
    .clk(Clock), .D(I6IN[1]), .Q(I6OUT[1]), .preset(Preset), .en(Enable), .reset(Clear));  // open: Qn
  D_Flip_Flop d_ff_99 (
    .clk(Clock), .D(I6IN[2]), .Q(I6OUT[2]), .preset(Preset), .en(Enable), .reset(Clear));  // open: Qn
  D_Flip_Flop d_ff_100 (
    .clk(Clock), .D(I6IN[3]), .Q(I6OUT[3]), .preset(Preset), .en(Enable), .reset(Clear));  // open: Qn
  D_Flip_Flop d_ff_101 (
    .clk(Clock), .D(I6IN[4]), .Q(I6OUT[4]), .preset(Preset), .en(Enable), .reset(Clear));  // open: Qn
  D_Flip_Flop d_ff_102 (
    .clk(Clock), .D(I6IN[5]), .Q(I6OUT[5]), .preset(Preset), .en(Enable), .reset(Clear));  // open: Qn
  D_Flip_Flop d_ff_103 (
    .clk(Clock), .D(I6IN[6]), .Q(I6OUT[6]), .preset(Preset), .en(Enable), .reset(Clear));  // open: Qn
  D_Flip_Flop d_ff_104 (
    .clk(Clock), .D(I6IN[7]), .Q(I6OUT[7]), .preset(Preset), .en(Enable), .reset(Clear));  // open: Qn
  D_Flip_Flop d_ff_105 (
    .clk(Clock), .D(I6IN[8]), .Q(I6OUT[8]), .preset(Preset), .en(Enable), .reset(Clear));  // open: Qn
  D_Flip_Flop d_ff_106 (
    .clk(Clock), .D(I6IN[9]), .Q(I6OUT[9]), .preset(Preset), .en(Enable), .reset(Clear));  // open: Qn
  D_Flip_Flop d_ff_107 (
    .clk(Clock), .D(I6IN[10]), .Q(I6OUT[10]), .preset(Preset), .en(Enable), .reset(Clear));  // open: Qn
  D_Flip_Flop d_ff_108 (
    .clk(Clock), .D(I6IN[11]), .Q(I6OUT[11]), .preset(Preset), .en(Enable), .reset(Clear));  // open: Qn
  D_Flip_Flop d_ff_109 (
    .clk(Clock), .D(I6IN[12]), .Q(I6OUT[12]), .preset(Preset), .en(Enable), .reset(Clear));  // open: Qn
  D_Flip_Flop d_ff_110 (
    .clk(Clock), .D(I6IN[13]), .Q(I6OUT[13]), .preset(Preset), .en(Enable), .reset(Clear));  // open: Qn
  D_Flip_Flop d_ff_111 (
    .clk(Clock), .D(I6IN[14]), .Q(I6OUT[14]), .preset(Preset), .en(Enable), .reset(Clear));  // open: Qn
  D_Flip_Flop d_ff_112 (
    .clk(Clock), .D(I6IN[15]), .Q(I6OUT[15]), .preset(Preset), .en(Enable), .reset(Clear));  // open: Qn
endmodule

module PC (
  input  I3,
  input  I4,
  input  I5,
  input  Clock,
  input  I6,
  input  C4,
  input  Preset,
  input  Enable,
  input  Clear,
  output S0,
  output S1,
  output S2,
  output S3
);

  wire Amarelo_out, and_1_out, and_2_out, and_3_out, and_4_out, and_5_out, and_6_out, Azul_E_out, Azul_out,
       Ciano_out, Laranja_out, \Lilás_out , Marrom_out, multiplexer_1_out, multiplexer_2_out,
       multiplexer_3_out, multiplexer_4_out, not_1_out, not_2_out, not_3_out, not_4_out, or_1_out, or_2_out,
       or_3_out, Verde_out;

  Multiplexer #(.disabled(0), .enable("false")) multiplexer_1 (
    .in0(or_1_out), .in1(I3), .out(multiplexer_1_out), .sel(C4));
  Multiplexer #(.disabled(0), .enable("false")) multiplexer_2 (
    .in0(or_2_out), .in1(I4), .out(multiplexer_2_out), .sel(C4));
  Multiplexer #(.disabled(0), .enable("false")) multiplexer_3 (
    .in0(or_3_out), .in1(I5), .out(multiplexer_3_out), .sel(C4));
  Multiplexer #(.disabled(0), .enable("false")) multiplexer_4 (
    .in0(not_4_out), .in1(I6), .out(multiplexer_4_out), .sel(C4));
  D_Flip_Flop d_ff_1 (
    .clk(Clock), .D(multiplexer_1_out), .Q(S3), .preset(Preset), .en(Enable), .reset(Clear));  // open: Qn
  D_Flip_Flop d_ff_2 (
    .clk(Clock), .D(multiplexer_2_out), .Q(S2), .preset(Preset), .en(Enable), .reset(Clear));  // open: Qn
  D_Flip_Flop d_ff_3 (
    .clk(Clock), .D(multiplexer_3_out), .Q(S1), .preset(Preset), .en(Enable), .reset(Clear));  // open: Qn
  D_Flip_Flop d_ff_4 (
    .clk(Clock), .D(multiplexer_4_out), .Q(S0), .preset(Preset), .en(Enable), .reset(Clear));  // open: Qn
  not not_1 (not_1_out, S3);
  not not_2 (not_2_out, S2);
  not not_3 (not_3_out, S1);
  not not_4 (not_4_out, S0);
  and and_1 (and_1_out, not_1_out, S2, S1, S0);
  and and_2 (and_2_out, S3, not_2_out, not_3_out, not_4_out);
  and Laranja (Laranja_out, S3, not_2_out, not_3_out, S0);
  and Verde (Verde_out, S3, not_2_out, S1, not_4_out);
  and \Lilás  (\Lilás_out , S3, not_2_out, S1, S0);
  and Azul_E (Azul_E_out, S3, S2, not_3_out, not_4_out);
  and Marrom (Marrom_out, S3, S2, not_3_out, S0);
  and Ciano (Ciano_out, S3, S2, S1, not_4_out);
  and and_3 (and_3_out, not_1_out, not_2_out, S1, S0);
  and and_4 (and_4_out, not_1_out, S2, not_3_out, not_4_out);
  and Azul (Azul_out, not_1_out, S2, not_3_out, S0);
  and Amarelo (Amarelo_out, not_1_out, S2, S1, not_4_out);
  and and_5 (and_5_out, not_1_out, not_2_out, not_3_out, S0);
  and and_6 (and_6_out, not_1_out, not_2_out, S1, not_4_out);
  or or_1 (or_1_out, and_1_out, and_2_out, Laranja_out, Verde_out, \Lilás_out , Azul_E_out, Marrom_out, Ciano_out);
  or or_2 (or_2_out, \Lilás_out , Azul_E_out, Marrom_out, Ciano_out, and_3_out, and_4_out, Azul_out, Amarelo_out);
  or or_3 (or_3_out, Laranja_out, Verde_out, Marrom_out, Ciano_out, Azul_out, Amarelo_out, and_5_out, and_6_out);
endmodule

module Somador_Completo (
  input  A,
  input  B,
  input  Ci,
  output S,
  output Co
);

  wire and_1_out, and_2_out, and_3_out, and_4_out, and_5_out, and_6_out, and_7_out, not_1_out, not_2_out,
       not_3_out;

  not not_1 (not_1_out, A);
  not not_2 (not_2_out, B);
  not not_3 (not_3_out, Ci);
  and and_1 (and_1_out, not_1_out, not_2_out, Ci);
  and and_2 (and_2_out, not_1_out, B, not_3_out);
  and and_3 (and_3_out, A, not_2_out, not_3_out);
  and and_4 (and_4_out, A, B, Ci);
  and and_5 (and_5_out, not_1_out, B, Ci);
  and and_6 (and_6_out, A, not_2_out, Ci);
  and and_7 (and_7_out, A, B, not_3_out);
  or or_1 (S, and_1_out, and_2_out, and_3_out, and_4_out);
  or or_2 (Co, and_4_out, and_5_out, and_6_out, and_7_out);
endmodule

module Controle (
  input  I0,
  input  I1,
  input  I2,
  input  SR,
  output C0,
  output C1,
  output C2,
  output C3,
  output C4
);

  wire and_1_out, and_2_out, and_4_out, not_1_out, not_2_out, not_3_out;

  not not_1 (not_1_out, I0);
  not not_2 (not_2_out, I1);
  not not_3 (not_3_out, I2);
  and and_1 (and_1_out, not_1_out, I1, not_3_out);
  and and_2 (and_2_out, I0, not_2_out, I2);
  and and_3 (C1, not_1_out, I1, I2);
  and and_4 (and_4_out, I0, not_2_out, not_3_out);
  or or_1 (C3, I0, not_2_out, I2);
  or or_2 (C0, and_1_out, and_2_out);
  or or_3 (C2, C1, and_4_out);
  and and_5 (C4, and_2_out, SR);
endmodule
